# Fritzing sketch voltage divider for bluetooth (saved by Fritzing 0.9.3b)
perfboards: 1

parts:
  R1 = Resistor [tolerance=±5% resistance=1k package=THT]
  R2 = Resistor [tolerance=±5% resistance=2k package=THT]

nets:
  N1: R1.Pin_1, R2.Pin_1

notes:
  Arduino & power
  HC-05 bluetooth
